// Logisim project circuitos_completos.circ as structural Verilog: 5 circuits, main circuit main
module main (
  input  F0,
  input  F1,
  input  F2,
  input  in_4,
  input  in_5,
  input  A3A2A1A0,
  input  in_7,
  input  in_8,
  input  ENA,
  input  in_10,
  input  B3B2B1B0,
  input  in_12,
  input  in_13,
  input  ENB,
  input  INC,
  output out_16,
  output out_17,
  output out_18,
  output out_19,
  output out_20,
  output out_21,
  output A_2,
  output B_2
);

  wire alu_2_out_11, alu_3_out_11, alu_4_out_11;

  Maior_que maior_que_1 (
    .F0(ENB), .F1(F1), .F2(F2), .A3(in_5), .B3(in_10), .A2(A3A2A1A0), .B2(B3B2B1B0), .A1(in_7), .B1(in_12),
    .A0(in_8), .B0(in_13), .out_12(out_21));
  ALU alu_1 (
    .INVA(in_4), .A(in_5), .ENA(ENA), .B(in_10), .ENB(ENB), .F0(ENB), .F1(F1), .F2(F2), .\Saída (out_17),
    .out_11(out_16), .Vem_um(alu_2_out_11));
  RestoPor2 restopor2_1 (.A0(in_8), .F0(ENB), .F1(F1), .F2(F2), .out_5(A_2));
  RestoPor2 restopor2_2 (.A0(in_13), .F0(ENB), .F1(F1), .F2(F2), .out_5(B_2));
  ALU alu_2 (
    .INVA(in_4), .A(A3A2A1A0), .ENA(ENA), .B(B3B2B1B0), .ENB(ENB), .F0(ENB), .F1(F1), .F2(F2),
    .\Saída (out_18), .out_11(alu_2_out_11), .Vem_um(alu_3_out_11));
  ALU alu_3 (
    .INVA(in_4), .A(in_7), .ENA(ENA), .B(in_12), .ENB(ENB), .F0(ENB), .F1(F1), .F2(F2), .\Saída (out_19),
    .out_11(alu_3_out_11), .Vem_um(alu_4_out_11));
  ALU alu_4 (
    .INVA(in_4), .A(in_8), .ENA(ENA), .B(in_13), .ENB(ENB), .F0(ENB), .F1(F1), .F2(F2), .\Saída (out_20),
    .out_11(alu_4_out_11), .Vem_um(INC));
  Maior_que maior_que_2 ();  // open: F0, F1, F2, A3, B3, A2, B2, A1, B1, A0, B0, out_12
  ALU alu_5 ();  // open: INVA, A, ENA, B, ENB, F0, F1, F2, Saída, out_11, Vem_um
  RestoPor2 restopor2_3 ();  // open: A0, F0, F1, F2, out_5

  assign F0 = ENB;

  // Notes on the sheet:
  //   INVA
  //   A
  //   B
  //   A Maior que
  //   Ordem
  //   INC
  //   F3
  //   INVA
  //   A
  //   ENA
  //   B
  //   ENB
  //   F0
  //   F1
  //   A0
  //   F0
  //   F1
  //   F2
  //   Saída
  //   Vai-um
  //   F0F1F2A3B3A2B2A1B1A0B0
endmodule

module ALU (
  input  Vem_um,
  input  INVA,
  input  A,
  input  ENA,
  input  B,
  input  ENB,
  input  F0,
  input  F1,
  input  F2,
  output \Saída ,
  output out_11
);

  wire and_1_out, and_2_out, and_3_out, and_4_out, and_5_out, and_6_out, and_11_out, and_12_out, and_13_out,
       and_14_out, and_15_out, and_16_out, and_17_out, not_1_out, not_2_out, not_3_out, not_4_out, not_5_out,
       not_6_out, not_7_out, not_8_out, or_1_out, xor_1_out, xor_2_out, xor_3_out;

  not not_1 (not_1_out, F0);
  not not_2 (not_2_out, F1);
  and and_1 (and_1_out, A, ENA);
  and and_2 (and_2_out, B, ENB);
  not not_3 (not_3_out, F0);
  not not_4 (not_4_out, F0);
  not not_5 (not_5_out, F1);
  not not_6 (not_6_out, F2);
  xor xor_1 (xor_1_out, INVA, and_1_out);
  not not_7 (not_7_out, F1);
  and and_3 (and_3_out, not_3_out, not_6_out, not_7_out);
  and and_4 (and_4_out, not_4_out, not_6_out, F1);
  and and_5 (and_5_out, F0, not_6_out, not_5_out);
  and and_6 (and_6_out, F0, not_6_out, F1);
  // AND_Gate and_7 has open pins: in0=not_1_out, in1=not_2_out, in4=F2, out=open
  // AND_Gate and_8 has open pins: in0=F0, in1=not_2_out, in4=F2, out=open
  // AND_Gate and_9 has open pins: in0=F1, in2=not_1_out, in4=F2, out=open
  // AND_Gate and_10 has open pins: in2=F0, in3=F1, in4=F2, out=open
  and and_11 (and_11_out, xor_1_out, and_2_out);
  or or_1 (or_1_out, xor_1_out, and_2_out);
  not not_8 (not_8_out, and_2_out);
  and and_12 (and_12_out, and_11_out, and_3_out);
  and and_13 (and_13_out, or_1_out, and_4_out);
  and and_14 (and_14_out, not_8_out, and_5_out);
  xor xor_2 (xor_2_out, and_2_out, xor_1_out);
  and and_15 (and_15_out, and_6_out, xor_1_out, and_2_out);
  or or_2 (out_11, and_15_out, and_16_out);
  and and_16 (and_16_out, and_6_out, xor_2_out, Vem_um);
  xor xor_3 (xor_3_out, Vem_um, xor_2_out);
  and and_17 (and_17_out, xor_3_out, and_6_out);
  or or_3 (\Saída , and_12_out, and_13_out, and_14_out, and_17_out);

  // Notes on the sheet:
  //   inc
  //   DECODIFICADOR
  //   f1
  //   f0
  //   Saída está nos circuitos fora da ALU
  //   UNIDADE LÓGICA
  //   AB
  //   A+B
  //   not B
  //   Somador Completo
  //   Soma
endmodule

module Maior_que (
  input  A3,
  input  B3,
  input  A2,
  input  B2,
  input  A1,
  input  B1,
  input  A0,
  input  B0,
  input  F0,
  input  F1,
  input  F2,
  output out_12
);

  wire and_1_out, and_2_out, and_3_out, and_4_out, and_6_out, and_7_out, and_8_out, and_9_out, not_1_out,
       not_2_out, not_3_out, not_4_out, not_5_out, not_6_out, or_1_out, xnor_1_out, xnor_2_out, xnor_3_out;

  and and_1 (and_1_out, A3, not_1_out);
  not not_1 (not_1_out, B3);
  not not_2 (not_2_out, F1);
  not not_3 (not_3_out, F0);
  xnor xnor_1 (xnor_1_out, A3, B3);
  and and_2 (and_2_out, A2, not_4_out);
  and and_3 (and_3_out, xnor_1_out, and_2_out);
  and and_4 (and_4_out, F2, not_2_out, not_3_out);
  not not_4 (not_4_out, B2);
  xnor xnor_2 (xnor_2_out, A2, B2);
  or or_1 (or_1_out, and_1_out, and_3_out, and_7_out, and_9_out);
  and and_5 (out_12, and_4_out, or_1_out);
  and and_6 (and_6_out, A1, not_5_out);
  and and_7 (and_7_out, xnor_1_out, xnor_2_out, and_6_out);
  not not_5 (not_5_out, B1);
  xnor xnor_3 (xnor_3_out, A1, B1);
  not not_6 (not_6_out, B0);
  and and_8 (and_8_out, A0, not_6_out);
  and and_9 (and_9_out, xnor_1_out, xnor_2_out, xnor_3_out, and_8_out);

  // Notes on the sheet:
  //   001 ATIVA MAIOR QUE
endmodule

module RestoPor2 (
  input  A0,
  input  F0,
  input  F1,
  input  F2,
  output out_5
);

  wire and_1_out, not_1_out;

  not not_1 (not_1_out, F0);
  and and_1 (and_1_out, A0, A0);
  and and_2 (out_5, and_1_out, not_1_out, F1, F2);

  // Notes on the sheet:
  //   0 1 1 Habilita resto da divisão por 2
  //   Verificar se A0 é 1.
  //   Caso seja, A0%2 = 1
  //   Caso contrário, 0
endmodule

module Igual (
  input  A3,
  input  B3,
  input  A2,
  input  B2,
  input  A1,
  input  B1,
  input  A0,
  input  B0,
  input  F0,
  input  F1,
  input  F2,
  output out_12
);

  wire and_1_out, and_2_out, and_3_out, and_4_out, xnor_1_out, xnor_2_out, xnor_3_out, xnor_4_out;

  xnor xnor_1 (xnor_1_out, A3, B3);
  and and_1 (and_1_out, xnor_1_out, xnor_2_out);
  xnor xnor_2 (xnor_2_out, A2, B2);
  and and_2 (and_2_out, F2, F1, F0);
  xnor xnor_3 (xnor_3_out, A1, B1);
  and and_3 (and_3_out, and_1_out, xnor_3_out);
  xnor xnor_4 (xnor_4_out, A0, B0);
  and and_4 (and_4_out, and_3_out, xnor_4_out);
  and and_5 (out_12, and_4_out, and_2_out);

  // Notes on the sheet:
  //   Circuito de igualdade
  //   Bits do decodificador 1 1 1
endmodule
